# Fritzing sketch arduino_lcd_tds (saved by Fritzing 1.0.6)
breadboards: 1

parts:
  Part1 = Arduino Uno (Rev3)
  S1 = PH meter [package=THT]
  LCD1 = LCD screen
  R1 = Trimmer Potentiometer [maximum_resistance=10kΩ knob_status=50% power=0.5W package=THT]
  LED1 = LED - 5mm [color="Red (633nm)" current=0.030A package="5 mm [THT]"]

nets:
  N1: Part1.A2, S1.pin1
  N2: Part1.D8, LCD1.E
  N3: Part1.D9_PWM, LCD1.DB4
  N4: Part1.D10_PWM/SS, LCD1.DB5
  N5: Part1.D11_PWM/MOSI, LCD1.DB6
  N6: Part1.D12/MISO, LCD1.DB7
  GND: Part1.GND, S1.pin3, LCD1.VSS, LCD1.R/W, LCD1.LED-, R1.leg2, LED1.cathode, LED1.anode
  N7: Part1.D7, LCD1.RS
  N8: Part1.3V3, S1.pin2
  5V: Part1.5V, LCD1.VDD, LCD1.LED+, R1.leg1
  N9: LCD1.V0, R1.wiper

// code stored in the sketch: arduino_lcd_tds-code.ino
#include <LiquidCrystal.h>
#define TdsSensorPin A1
#define VREF 5.0
#define SCOUNT 30

int analogBuffer[SCOUNT];
int analogBufferTemp[SCOUNT];
int analogBufferIndex = 0, copyIndex = 0;
LiquidCrystal lcd(7, 8, 9, 10, 11, 12);

float averageVoltage = 0;
float tdsValue = 0;
float temperature = 25;

void setup() { 
  lcd.begin(16, 2);
  pinMode(TdsSensorPin, INPUT);
} 

void loop() { 
  static unsigned long analogSampleTimepoint = millis();

  if (millis() - analogSampleTimepoint > 40U) {
    analogSampleTimepoint = millis();
    analogBuffer[analogBufferIndex] = analogRead(TdsSensorPin);
    analogBufferIndex++;
    if (analogBufferIndex == SCOUNT) analogBufferIndex = 0;
  }

  static unsigned long printTimepoint = millis();

  if (millis() - printTimepoint > 800U) {
    printTimepoint = millis();

    for (copyIndex = 0; copyIndex < SCOUNT; copyIndex++)
      analogBufferTemp[copyIndex] = analogBuffer[copyIndex];

    averageVoltage = getMedianNum(analogBufferTemp, SCOUNT) * (float)VREF / 1024.0;

    float compensationCoefficient = 1.0 + 0.02 * (temperature - 25.0);
    float compensationVoltage = averageVoltage / compensationCoefficient;

    tdsValue = (133.42 * compensationVoltage * compensationVoltage * compensationVoltage
               - 255.86 * compensationVoltage * compensationVoltage
               + 857.39 * compensationVoltage) * 0.5;
    lcd.setCursor(0, 0);
    lcd.print("TDS value:");
    lcd.setCursor(0, 1);
    lcd.print(tdsValue, 0);
    lcd.print(" ppm");
  }
}

int getMedianNum(int bArray[], int iFilterLen) {
  int bTab[iFilterLen];

  for (byte i = 0; i < iFilterLen; i++)
    bTab[i] = bArray[i];

  int i, j, bTemp;

  for (j = 0; j < iFilterLen - 1; j++) {
    for (i = 0; i < iFilterLen - j - 1; i++) {
      if (bTab[i] > bTab[i + 1]) {
        bTemp = bTab[i];
        bTab[i] = bTab[i + 1];
        bTab[i + 1] = bTemp;
      }
    }
  }

  if ((iFilterLen & 1) > 0)
    bTemp = bTab[(iFilterLen - 1) / 2];
  else
    bTemp = (bTab[iFilterLen / 2] + bTab[iFilterLen / 2 - 1]) / 2;

  return bTemp;
}
